// Logisim project C-ControlUnit.circ as structural Verilog: 1 circuit, main circuit ControlUnit
module ControlUnit (
  input  in_1,
  input  in_2,
  input  End_Fectch_Instruction,
  input  Instruction_Avaiable,
  output Start_Fectch_Instruction,
  output LoadInstructionRegister
);

  wire d_ff_1_q, demultiplexer_1_out1, demultiplexer_2_out0, demultiplexer_2_out1, END_q, or_1_out, or_2_out,
       or_3_out, Wait_for_instruction_fetch_q;

  or or_1 (or_1_out, 1'b0, demultiplexer_1_out1);
  Demultiplexer #(.enable("false")) demultiplexer_1 (
    .out0(Start_Fectch_Instruction), .out1(demultiplexer_1_out1), .in(d_ff_1_q), .sel(in_1));
  D_Flip_Flop d_ff_1 (.clk(in_2), .D(or_1_out), .Q(d_ff_1_q), .preset(in_1));  // open: Qn, en, reset
  D_Flip_Flop Wait_for_instruction_fetch (
    .clk(in_2), .D(or_2_out), .Q(Wait_for_instruction_fetch_q), .reset(in_1));  // open: Qn, preset, en
  or or_2 (or_2_out, demultiplexer_2_out0, Start_Fectch_Instruction);
  Demultiplexer #(.enable("false")) demultiplexer_2 (
    .out0(demultiplexer_2_out0), .out1(demultiplexer_2_out1), .in(Wait_for_instruction_fetch_q),
    .sel(End_Fectch_Instruction));
  D_Flip_Flop END (.clk(in_2), .D(or_3_out), .Q(END_q), .reset(in_1));  // open: Qn, preset, en
  or or_3 (or_3_out, END_q, demultiplexer_2_out1);

  assign LoadInstructionRegister = Instruction_Avaiable;

  // Other names for the same wires on the sheet: CLK = in_2; End_fetch_instruction = End_Fectch_Instruction;
  //   Instruction_ready = Instruction_Avaiable; RST = in_1; Start_fetch_instruction = Start_Fectch_Instruction

  // Notes on the sheet:
  //   FetchInstruction
  //   Control Signals
  //   Fetch Instruction
endmodule
